# Fritzing sketch circuit (saved by Fritzing 0.9.10b)

parts:
  Part1 = Arduino Uno (Rev3)
  M1 = GY-MAX30102

nets:
  N1: Part1.A4/SDA, M1.SDA
  N2: Part1.A5/SCL, M1.SCL
  5V: Part1.5V, M1.VIN
  GND: Part1.GND, M1.GND

custom parts:
  GY-MAX30102: Oximeter module using the MAX30102 chip. You may wish to read (and check your module) this post on power problems with these modules: https://reedpaper.wordpress.com/2018/08/22/pulse-oximeter-max30100-max30102-how-to-fix-wrong-board/ (may not apply as this is a different module!). As usual, if you want the mounting holes in pcb, you need to drag a hole over the pad in silkscreen to actually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
